# Fritzing sketch PIRServo (saved by Fritzing 0.9.3b)
breadboards: 1

parts:
  Arduino_UNO = Arduino Uno (Rev3)
  PIR1 = PIR sensor
  J1 = Basic Servo

nets:
  N1: Arduino_UNO.A3, PIR1.SIG
  GND: Arduino_UNO.GND, PIR1.GND, J1.gnd
  N2: Arduino_UNO.D5_PWM, J1.pulse
  5V: Arduino_UNO.5V, PIR1.VDD, J1.vcc
