# Fritzing sketch thermistor_fan (saved by Fritzing 0.8.7b)
breadboards: 1

parts:
  Arduino = Arduino Uno (Rev3)
  R1 = Resistor [tolerance=±5% resistance=10k package=THT]
  R2 = Temperature Sensor (Thermistor) [thermistor_type=NTC package=THT]
  R3 = Resistor [tolerance=±5% resistance=220 package=THT]
  C1 = Ceramic Capacitor [capacitance=100nF package="100 mil [THT, multilayer]"]
  D1 = Diode [package=diode-1n4148]
  Motor = DC Motor
  Q1 = NPN-Transistor [package="TO92 [THT]"]

nets:
  N1: Arduino.A0, R1.Pin_0, R2.pin_1
  N2: Arduino.D13/SCK, R3.Pin_0
  N3: Arduino.5V, R2.pin_0, C1.0, D1.A, Motor.pin_2
  N4: Arduino.GND, R1.Pin_1, Q1.E
  N5: R3.Pin_1, Q1.B
  N6: C1.1, D1.C, Motor.pin_1, Q1.C
