# Fritzing sketch yepclock (saved by Fritzing 0.8.7b)
breadboards: 1

parts:
  LCD = LCD screen
  Rotary_Encoder = Rotary Encoder [package=THT]
  R2 = Resistor [tolerance=±5% resistance=220 package=THT]
  Arduino = Arduino Uno (Rev3)
  Switch = Pushbutton [package="[THT]"]
  RTC = Real Time Clock Module - DS1307 RTC Breakout Board
  R1 = Rotary Potentiometer (Small) [maximum_resistance=10kΩ package=THT]
  Buzzer = Piezo Speaker

nets:
  GND: LCD.VSS, LCD.R/W, LCD.LED-, Rotary_Encoder.EncoderPinC, Arduino.GND, Switch.Pin_1, Switch.Pin_2, RTC.GND, R1.leg2, Buzzer.pin1
  5V: LCD.VDD, R2.Pin_0, Arduino.5V, RTC.5V, R1.leg1
  N1: LCD.V0, R1.wiper
  N2: LCD.RS, Arduino.D6_PWM
  N3: LCD.E, Arduino.D7
  N4: LCD.DB4, Arduino.D8
  N5: LCD.DB5, Arduino.D9_PWM
  N6: LCD.DB6, Arduino.D10_PWM/SS
  N7: LCD.DB7, Arduino.D11_PWM/MOSI
  N8: LCD.LED+, R2.Pin_1
  N9: Rotary_Encoder.EncoderPinA, Arduino.D3_PWM
  N10: Rotary_Encoder.EncoderPinB, Arduino.D4
  N11: Arduino.A4/SDA, RTC.SDA
  N12: Arduino.D12/MISO, Buzzer.pin2
  N13: Arduino.A5/SCL, RTC.SCL
  N14: Arduino.D2, Switch.Pin_3, Switch.Pin_4
